// Logisim project CRC(1).circ as structural Verilog: 2 circuits, main circuit CRC
module _4bit_mod (
  input  [3:0] A,
  input  [3:0] B,
  output D,
  output [2:0] C
);

  wire [3:0] xor_1_out;
  wire [3:3] multiplexer_1_out;

  assign xor_1_out = A ^ B;  // XOR_Gate xor_1, 4 bits wide
  Multiplexer #(.width(4), .enable("false")) multiplexer_1 (
    .in0(A), .in1(xor_1_out), .out({multiplexer_1_out[3], C}), .sel(A[3]));

  assign D = A[3];
endmodule

module CRC (
  input  [7:0] A,
  input  [3:0] B,
  output [10:0] C
);

  wire Q1, Q2, Q3, Q4, Q5, Q6, Q7, Q8;
  wire [2:0] n4bit_mod_1_c, n4bit_mod_2_c, n4bit_mod_3_c, n4bit_mod_4_c, n4bit_mod_5_c, R3, R6;

  _4bit_mod u_4bit_mod_1 (.A(A[7:4]), .B(B), .D(Q1), .C(n4bit_mod_1_c));
  _4bit_mod u_4bit_mod_2 (.A({R3, A[1]}), .B(B), .D(Q4), .C(n4bit_mod_2_c));
  _4bit_mod u_4bit_mod_3 (.A({R6, 1'b0}), .B(B), .D(Q7), .C(n4bit_mod_3_c));
  _4bit_mod u_4bit_mod_4 (.A({n4bit_mod_1_c, A[3]}), .B(B), .D(Q2), .C(n4bit_mod_4_c));
  _4bit_mod u_4bit_mod_5 (.A({n4bit_mod_2_c, A[0]}), .B(B), .D(Q5), .C(n4bit_mod_5_c));
  _4bit_mod u_4bit_mod_6 (.A({n4bit_mod_3_c, 1'b0}), .B(B), .D(Q8), .C(C[2:0]));
  _4bit_mod u_4bit_mod_7 (.A({n4bit_mod_4_c, A[2]}), .B(B), .D(Q3), .C(R3));
  _4bit_mod u_4bit_mod_8 (.A({n4bit_mod_5_c, 1'b0}), .B(B), .D(Q6), .C(R6));

  assign C[10:3] = A;

  // Other names for the same wires on the sheet: _3 = A[2]; R8[2:0] = C[2:0]; _5 = A[0]; _4 = A[1]; _2 = A[3];
  //   _1[3:0] = A[7:4]

  // Notes on the sheet:
  //   yuanshuju
endmodule
