// Logisim project FSM.circ as structural Verilog: 3 circuits, main circuit fsm
module fsm (
  input  [1:0] In,
  input  CLR,
  output Out
);

  wire clock_1_out;
  wire [2:0] multiplexer_1_out, register_1_q, transfer_1_snew;

  transfer transfer_1 (.In(In), .S(register_1_q), .Snew(transfer_1_snew));
  Multiplexer #(.width(3), .enable("false")) multiplexer_1 (
    .in0(transfer_1_snew), .in1(3'b000), .out(multiplexer_1_out), .sel(CLR));
  Register #(.width(3)) register_1 (.D(multiplexer_1_out), .Q(register_1_q), .clk(clock_1_out));  // open: en, clr
  Clock clock_1 (.out(clock_1_out));
  out out_1 (.In(In), .S(register_1_q), .Out(Out));
endmodule

module transfer (
  input  [1:0] In,
  input  [2:0] S,
  output [2:0] Snew
);

  wire and_2_out, and_3_out, and_4_out, and_5_out, and_6_out, and_7_out, and_8_out, not_1_out, not_2_out,
       not_3_out, not_4_out, not_5_out, not_6_out, not_7_out, not_8_out, not_9_out, not_10_out, not_11_out,
       not_12_out, not_13_out, not_14_out;

  not not_1 (not_1_out, In[0]);
  not not_2 (not_2_out, In[1]);
  not not_3 (not_3_out, S[1]);
  not not_4 (not_4_out, In[0]);
  not not_5 (not_5_out, S[1]);
  not not_6 (not_6_out, In[0]);
  not not_7 (not_7_out, S[0]);
  not not_8 (not_8_out, In[0]);
  not not_9 (not_9_out, S[1]);
  not not_10 (not_10_out, In[0]);
  not not_11 (not_11_out, S[0]);
  not not_12 (not_12_out, In[1]);
  not not_13 (not_13_out, S[0]);
  not not_14 (not_14_out, In[1]);
  and and_1 (Snew[2], not_1_out, S[1], S[0]);
  and and_2 (and_2_out, not_2_out, not_3_out, S[0]);
  and and_3 (and_3_out, not_4_out, not_5_out, S[0]);
  and and_4 (and_4_out, not_6_out, S[1], not_7_out);
  and and_5 (and_5_out, not_8_out, not_9_out, S[0]);
  and and_6 (and_6_out, not_10_out, S[1], not_11_out);
  and and_7 (and_7_out, not_12_out, In[0], not_13_out);
  and and_8 (and_8_out, not_14_out, In[0], S[1]);
  or or_1 (Snew[1], and_2_out, and_3_out, and_4_out);
  or or_2 (Snew[0], and_5_out, and_6_out, and_7_out, and_8_out);
endmodule

module out (
  input  [1:0] In,
  input  [2:0] S,
  output Out
);

  wire not_1_out;

  not not_1 (not_1_out, In[0]);
  and and_1 (Out, not_1_out, S[1], S[0]);
endmodule
