// Logisim project P0_L4.circ as structural Verilog: 1 circuit, main circuit interview
module interview (
  input  [2:0] standard,
  input  [2:0] tea,
  input  [1:0] S1,
  input  [1:0] S2,
  output out_5
);

  wire comparator_1_gt, comparator_2_eq;
  wire [4:0] adder_1_out, S1_t, S2_t, standard_t, tea_t, total;

  assign standard_t = {{2{1'b0}}, standard};  // Bit_Extender bit_extender_1
  assign tea_t = {{2{1'b0}}, tea};  // Bit_Extender bit_extender_2
  assign S1_t = {{3{1'b0}}, S1};  // Bit_Extender bit_extender_3
  assign S2_t = {{3{1'b0}}, S2};  // Bit_Extender bit_extender_4
  Adder #(.width(5)) adder_1 (.a(S1_t), .b(S2_t), .out(adder_1_out));  // open: cin, cout
  Adder #(.width(5)) adder_2 (.a(adder_1_out), .b(tea_t), .out(total));  // open: cin, cout
  Comparator #(.width(5), .mode("unsigned")) comparator_1 (
    .a(total), .b(standard_t), .gt(comparator_1_gt));  // open: eq, lt
  Comparator #(.width(5), .mode("unsigned")) comparator_2 (
    .a(tea_t), .b({5{1'b0}}), .eq(comparator_2_eq));  // open: gt, lt
  Multiplexer multiplexer_1 (.in0(comparator_1_gt), .in1(1'b0), .out(out_5), .sel(comparator_2_eq));  // open: en
endmodule
