// Logisim project P0_L5.circ as structural Verilog: 1 circuit, main circuit dtoo
module dtoo (
  input  [3:0] high_in,
  input  [3:0] low_in,
  output [1:0] high_out,
  output [2:0] mid_out,
  output [2:0] low_out
);

  wire [7:0] bit_extender_1_out, bit_extender_2_out, multiplier_1_out;

  assign bit_extender_1_out = {{4{1'b0}}, high_in};  // Bit_Extender bit_extender_1
  assign bit_extender_2_out = {{4{1'b0}}, low_in};  // Bit_Extender bit_extender_2
  // Probe on multiplier_1_out
  Multiplier multiplier_1 (.a(bit_extender_1_out), .b(8'ha), .out(multiplier_1_out));  // open: cin, cout
  Adder adder_1 (.a(multiplier_1_out), .b(bit_extender_2_out), .out({high_out, mid_out, low_out}));  // open: cin, cout
  // Probe on {high_out, mid_out, low_out}

  // Other names for the same wires on the sheet: 处理好的二进制[7:0] = {high_out, mid_out, low_out}
endmodule
