// Logisim project P0课上fibonacci.circ as structural Verilog: 2 circuits, main circuit main
module main (
  input  in_1,
  input  [4:0] \input ,
  output [31:0] \output 
);

  wire CLK, comparator_1_lt, comparator_2_gt, counter_2_q, counter_3_q, freeze, \判断1 ;
  wire [5:0] bit_extender_1_out, counter;
  wire [31:0] _3, adder_1_out, adder_2_out, multiplexer_2_out, multiplexer_3_out, xor_1_out, xor_2_out, \寄2 ,
       \寄3 ;

  Counter #(.width(6), .max('h3f), .ongoal("stay")) counter_1 (
    .Q(counter), .clk(CLK), .clr(in_1));  // open: load, D, count, carry
  Clock clock_1 (.out(CLK));
  // Probe on counter
  Counter #(.width(1), .max('h1)) counter_2 (.Q(counter_2_q), .clk(CLK), .clr(in_1));  // open: load, D, count, carry
  Multiplexer #(.width(32)) multiplexer_1 (.in0({32{1'b0}}), .in1(32'h1), .out(_3), .sel(counter_2_q));  // open: en
  Register #(.width(32)) \u_寄1  (.D(multiplexer_3_out), .Q(\output ), .clk(CLK), .clr(in_1));  // open: en
  assign xor_1_out = \寄2  ^ \寄3 ;  // XOR_Gate xor_1, 32 bits wide
  assign xor_2_out = \output  ^ \寄2 ;  // XOR_Gate xor_2, 32 bits wide
  Adder #(.width(32)) adder_1 (.a(xor_1_out), .b(\output ), .out(adder_1_out));  // open: cin, cout
  Adder #(.width(32)) adder_2 (.a(xor_2_out), .b(\寄3 ), .out(adder_2_out));  // open: cin, cout
  Register #(.width(32)) \u_寄2  (.D(\output ), .Q(\寄2 ), .clk(CLK), .clr(in_1));  // open: en
  Multiplexer #(.width(32)) multiplexer_2 (
    .in0(adder_1_out), .in1(adder_2_out), .out(multiplexer_2_out), .sel(counter_3_q));  // open: en
  Counter #(.width(1), .max('h1)) counter_3 (.Q(counter_3_q), .clk(CLK), .clr(in_1));  // open: load, D, count, carry
  Multiplexer #(.width(32)) multiplexer_3 (
    .in0(_3), .in1(multiplexer_2_out), .out(multiplexer_3_out), .sel(\判断1 ), .en(freeze));
  assign bit_extender_1_out = {{1{1'b0}}, \input };  // Bit_Extender bit_extender_1
  Register #(.width(32)) \u_寄3  (.D(\寄2 ), .Q(\寄3 ), .clk(CLK), .clr(in_1));  // open: en
  Comparator #(.width(6), .mode("unsigned")) comparator_1 (
    .a(counter), .b(6'b000011), .lt(comparator_1_lt));  // open: gt, eq
  Comparator #(.width(6), .mode("unsigned")) comparator_2 (
    .a(counter), .b(bit_extender_1_out), .gt(comparator_2_gt));  // open: eq, lt
  not not_1 (freeze, comparator_2_gt);
  // Probe on \判断1 
  not not_2 (\判断1 , comparator_1_lt);
  // Probe on freeze

  // Other names for the same wires on the sheet: Reset = in_1; 寄1[31:0] = \output 
endmodule

module \测试电路图  (
  input  [4:0] in_1,
  input  in_2,
  output [31:0] out_3
);

  wire clock_1_out;
  wire [7:0] counter_1_q;

  Counter counter_1 (.Q(counter_1_q), .clk(clock_1_out), .clr(in_2));  // open: load, D, count, carry
  Clock clock_1 (.out(clock_1_out));
  main main_1 (.\input (in_1), .\output (out_3));  // open: in_1
  // Probe on counter_1_q
endmodule
