// Logisim project P0课上q1.circ as structural Verilog: 1 circuit, main circuit main
module main (
  input  [1:0] s,
  input  [1:0] ig,
  input  [1:0] t0,
  input  [1:0] t1,
  input  [1:0] t2,
  input  [1:0] t3,
  output result
);

  wire decoder_1_out0, decoder_1_out1, decoder_1_out3, decoder_2_out0, decoder_2_out1, decoder_2_out3,
       decoder_3_out0, decoder_3_out1, decoder_3_out3, decoder_4_out0, decoder_4_out1, decoder_4_out3,
       decoder_5_out0, decoder_5_out1, decoder_5_out3, demultiplexer_1_out0, demultiplexer_1_out1,
       demultiplexer_1_out2, demultiplexer_1_out3, demultiplexer_1_out4, or_1_out, or_2_out, or_3_out,
       or_4_out, t0enable, t1enable, t2enable, t3enable;
  wire [2:0] ig_t, igenable;
  wire [3:0] adder_1_out, adder_2_out, adder_3_out, adder_4_out, adder_5_out, adder_6_out, adder_7_out,
       adder_8_out, bit_extender_2_out, bit_extender_3_out, bit_extender_4_out, bit_extender_5_out,
       bit_extender_6_out, bit_extender_7_out, bit_extender_8_out, bit_extender_9_out, bit_extender_10_out,
       bit_extender_11_out;

  Decoder #(.select(2)) decoder_1 (
    .out0(decoder_1_out0), .out1(decoder_1_out1), .out3(decoder_1_out3), .sel(s));  // open: out2, en
  assign ig_t = {{1{1'b0}}, ig};  // Bit_Extender bit_extender_1
  Decoder #(.select(2), .disabled(0)) decoder_2 (
    .out0(decoder_2_out0), .out1(decoder_2_out1), .out3(decoder_2_out3), .sel(t0), .en(t0enable));  // open: out2
  Decoder #(.select(2), .disabled(0)) decoder_3 (
    .out0(decoder_3_out0), .out1(decoder_3_out1), .out3(decoder_3_out3), .sel(t1), .en(t1enable));  // open: out2
  Decoder #(.select(2), .disabled(0)) decoder_4 (
    .out0(decoder_4_out0), .out1(decoder_4_out1), .out3(decoder_4_out3), .sel(t2), .en(t2enable));  // open: out2
  Decoder #(.select(2), .disabled(0)) decoder_5 (
    .out0(decoder_5_out0), .out1(decoder_5_out1), .out3(decoder_5_out3), .sel(t3), .en(t3enable));  // open: out2
  Demultiplexer #(.select(3)) demultiplexer_1 (
    .out0(demultiplexer_1_out0), .out1(demultiplexer_1_out1), .out2(demultiplexer_1_out2),
    .out3(demultiplexer_1_out3), .out4(demultiplexer_1_out4), .in(1'b1), .sel(igenable));  // open: out5, out6, out7, en
  assign bit_extender_2_out = {{3{1'b0}}, decoder_1_out0};  // Bit_Extender bit_extender_2
  assign bit_extender_3_out = {{3{1'b0}}, decoder_1_out1};  // Bit_Extender bit_extender_3
  Multiplexer #(.width(3)) multiplexer_1 (.in0(3'b100), .in1(ig_t), .out(igenable), .sel(decoder_1_out3));  // open: en
  or or_1 (or_1_out, decoder_2_out1, decoder_2_out3);
  or or_2 (or_2_out, decoder_3_out1, decoder_3_out3);
  or or_3 (or_3_out, decoder_4_out1, decoder_4_out3);
  or or_4 (or_4_out, decoder_5_out1, decoder_5_out3);
  not not_1 (t0enable, demultiplexer_1_out0);
  not not_2 (t1enable, demultiplexer_1_out1);
  not not_3 (t2enable, demultiplexer_1_out2);
  not not_4 (t3enable, demultiplexer_1_out3);
  assign bit_extender_4_out = {{3{1'b0}}, decoder_2_out0};  // Bit_Extender bit_extender_4
  assign bit_extender_5_out = {{3{1'b0}}, or_1_out};  // Bit_Extender bit_extender_5
  assign bit_extender_6_out = {{3{1'b0}}, decoder_3_out0};  // Bit_Extender bit_extender_6
  assign bit_extender_7_out = {{3{1'b0}}, or_2_out};  // Bit_Extender bit_extender_7
  assign bit_extender_8_out = {{3{1'b0}}, decoder_4_out0};  // Bit_Extender bit_extender_8
  assign bit_extender_9_out = {{3{1'b0}}, or_3_out};  // Bit_Extender bit_extender_9
  assign bit_extender_10_out = {{3{1'b0}}, decoder_5_out0};  // Bit_Extender bit_extender_10
  assign bit_extender_11_out = {{3{1'b0}}, or_4_out};  // Bit_Extender bit_extender_11
  Adder #(.width(4)) adder_1 (.a(bit_extender_4_out), .b(bit_extender_6_out), .out(adder_1_out));  // open: cin, cout
  Adder #(.width(4)) adder_2 (.a(bit_extender_5_out), .b(bit_extender_7_out), .out(adder_2_out));  // open: cin, cout
  Adder #(.width(4)) adder_3 (.a(adder_2_out), .b(bit_extender_9_out), .out(adder_3_out));  // open: cin, cout
  Adder #(.width(4)) adder_4 (.a(adder_1_out), .b(bit_extender_8_out), .out(adder_4_out));  // open: cin, cout
  Adder #(.width(4)) adder_5 (.a(adder_4_out), .b(bit_extender_10_out), .out(adder_5_out));  // open: cin, cout
  Adder #(.width(4)) adder_6 (.a(adder_3_out), .b(bit_extender_11_out), .out(adder_6_out));  // open: cin, cout
  Adder #(.width(4)) adder_7 (.a(adder_5_out), .b(bit_extender_2_out), .out(adder_7_out));  // open: cin, cout
  Adder #(.width(4)) adder_8 (.a(adder_6_out), .b(bit_extender_3_out), .out(adder_8_out));  // open: cin, cout
  Comparator #(.width(4)) comparator_1 (.a(adder_7_out), .b(adder_8_out), .gt(result));  // open: eq, lt
endmodule
