// Logisim project P0课上q2.circ as structural Verilog: 3 circuits, main circuit main
module main (
  input  [1:0] in_1,
  input  in_2,
  output [1:0] out_3
);

  wire clock_1_out;
  wire [3:0] register_1_q, state_transform_1_s0_;

  state_transform state_transform_1 (
    .S3(register_1_q[3]), .S2(register_1_q[2]), .S1(register_1_q[1]), .S0(register_1_q[0]), .in1(in_1[1]),
    .in0(in_1[0]), .S3_(state_transform_1_s0_[3]), .S2_(state_transform_1_s0_[2]),
    .S1_(state_transform_1_s0_[1]), .S0_(state_transform_1_s0_[0]));
  Register #(.width(4)) register_1 (
    .D(state_transform_1_s0_), .Q(register_1_q), .clk(clock_1_out), .clr(in_2));  // open: en
  Clock clock_1 (.out(clock_1_out));
  state_output state_output_1 (
    .S3(register_1_q[3]), .S2(register_1_q[2]), .S1(register_1_q[1]), .S0(register_1_q[0]), .in1(in_1[1]),
    .in0(in_1[0]), .out1(out_3[1]), .out0(out_3[0]));
endmodule

module state_transform (
  input  S3,
  input  S2,
  input  S1,
  input  S0,
  input  in1,
  input  in0,
  output S3_,
  output S2_,
  output S1_,
  output S0_
);

  wire and_1_out, and_2_out, and_3_out, and_4_out, and_5_out, and_6_out, and_7_out, and_8_out, and_9_out,
       and_10_out, and_11_out, and_12_out, and_13_out, and_14_out, and_15_out, and_16_out, and_17_out,
       and_18_out, and_19_out, and_20_out, not_1_out, not_2_out, not_3_out, not_4_out, not_5_out, not_6_out,
       not_7_out, not_8_out, not_9_out, not_10_out, not_11_out, not_12_out, not_13_out, not_14_out,
       not_15_out, not_16_out, not_17_out, not_18_out, not_19_out, not_20_out, not_21_out, not_22_out,
       not_23_out, not_24_out, not_25_out, not_26_out, not_27_out, not_28_out, not_29_out, not_30_out,
       not_31_out, not_32_out, not_33_out, not_34_out, not_35_out, not_36_out, not_37_out, not_38_out,
       not_39_out, not_40_out, not_41_out, not_42_out, not_43_out, not_44_out, not_45_out, not_46_out,
       not_47_out, not_48_out, not_49_out, not_50_out, not_51_out, not_52_out, not_53_out, not_54_out,
       not_55_out, not_56_out, not_57_out, not_58_out, not_59_out, not_60_out, not_61_out, not_62_out,
       not_63_out, not_64_out, not_65_out, not_66_out;

  not not_1 (not_1_out, S3);
  not not_2 (not_2_out, S1);
  not not_3 (not_3_out, S0);
  not not_4 (not_4_out, in1);
  not not_5 (not_5_out, in0);
  not not_6 (not_6_out, S3);
  not not_7 (not_7_out, in1);
  not not_8 (not_8_out, in0);
  not not_9 (not_9_out, S3);
  not not_10 (not_10_out, S0);
  not not_11 (not_11_out, in1);
  not not_12 (not_12_out, S3);
  not not_13 (not_13_out, in1);
  not not_14 (not_14_out, S3);
  not not_15 (not_15_out, in1);
  not not_16 (not_16_out, S3);
  not not_17 (not_17_out, S1);
  not not_18 (not_18_out, in0);
  not not_19 (not_19_out, S3);
  not not_20 (not_20_out, in0);
  not not_21 (not_21_out, S3);
  not not_22 (not_22_out, S2);
  not not_23 (not_23_out, S1);
  not not_24 (not_24_out, in1);
  not not_25 (not_25_out, S3);
  not not_26 (not_26_out, S2);
  not not_27 (not_27_out, S0);
  not not_28 (not_28_out, in0);
  not not_29 (not_29_out, S3);
  not not_30 (not_30_out, S1);
  not not_31 (not_31_out, in0);
  not not_32 (not_32_out, S3);
  not not_33 (not_33_out, in0);
  not not_34 (not_34_out, S3);
  not not_35 (not_35_out, S0);
  not not_36 (not_36_out, in1);
  not not_37 (not_37_out, S2);
  not not_38 (not_38_out, S1);
  not not_39 (not_39_out, S0);
  not not_40 (not_40_out, in1);
  not not_41 (not_41_out, S3);
  not not_42 (not_42_out, S2);
  not not_43 (not_43_out, S0);
  not not_44 (not_44_out, in1);
  not not_45 (not_45_out, S3);
  not not_46 (not_46_out, S2);
  not not_47 (not_47_out, in1);
  not not_48 (not_48_out, in0);
  not not_49 (not_49_out, S2);
  not not_50 (not_50_out, S1);
  not not_51 (not_51_out, S0);
  not not_52 (not_52_out, in1);
  not not_53 (not_53_out, in0);
  not not_54 (not_54_out, S3);
  not not_55 (not_55_out, S1);
  not not_56 (not_56_out, in1);
  not not_57 (not_57_out, in0);
  not not_58 (not_58_out, S3);
  not not_59 (not_59_out, S2);
  not not_60 (not_60_out, S0);
  not not_61 (not_61_out, in0);
  not not_62 (not_62_out, S3);
  not not_63 (not_63_out, S0);
  not not_64 (not_64_out, in1);
  not not_65 (not_65_out, S3);
  not not_66 (not_66_out, in1);
  and and_1 (and_1_out, not_1_out, S2, not_2_out, not_3_out, not_4_out, not_5_out);
  and and_2 (and_2_out, not_6_out, S2, S1, S0, not_7_out, not_8_out);
  and and_3 (and_3_out, not_9_out, not_10_out, not_11_out, in0);
  and and_4 (and_4_out, not_12_out, S1, not_13_out, in0);
  and and_5 (and_5_out, not_14_out, S2, not_15_out, in0);
  and and_6 (and_6_out, not_16_out, S2, not_17_out, in1, not_18_out);
  and and_7 (and_7_out, not_19_out, S2, S0, in1, not_20_out);
  and and_8 (and_8_out, not_21_out, not_22_out, not_23_out, S0, not_24_out, in0);
  and and_9 (and_9_out, not_25_out, not_26_out, S1, not_27_out, in1, not_28_out);
  and and_10 (and_10_out, not_29_out, S2, not_30_out, in1, not_31_out);
  and and_11 (and_11_out, not_32_out, S2, S0, in1, not_33_out);
  and and_12 (and_12_out, not_34_out, S2, S1, not_35_out, not_36_out, in0);
  and and_13 (and_13_out, S3, not_37_out, not_38_out, not_39_out, not_40_out, in0);
  and and_14 (and_14_out, not_41_out, not_42_out, not_43_out, not_44_out);
  and and_15 (and_15_out, not_45_out, not_46_out, not_47_out, not_48_out);
  and and_16 (and_16_out, not_49_out, not_50_out, not_51_out, not_52_out, not_53_out);
  and and_17 (and_17_out, not_54_out, not_55_out, S0, not_56_out, not_57_out);
  and and_18 (and_18_out, not_58_out, not_59_out, S1, not_60_out, not_61_out);
  and and_19 (and_19_out, not_62_out, S1, not_63_out, not_64_out);
  and and_20 (and_20_out, not_65_out, S2, not_66_out, in0);
  or or_1 (S3_, and_1_out, and_2_out);
  or or_2 (S2_, and_3_out, and_4_out, and_5_out, and_6_out, and_7_out);
  or or_3 (S1_, and_8_out, and_9_out, and_10_out, and_11_out, and_12_out, and_13_out);
  or or_4 (S0_, and_14_out, and_15_out, and_16_out, and_17_out, and_18_out, and_19_out, and_20_out);
endmodule

module state_output (
  input  S3,
  input  S2,
  input  S1,
  input  S0,
  input  in1,
  input  in0,
  output out1,
  output out0
);

  wire and_1_out, and_2_out, not_1_out, not_2_out, not_3_out, not_4_out, not_5_out, not_6_out, not_7_out,
       not_8_out, not_9_out, not_10_out, not_11_out;

  not not_1 (not_1_out, S3);
  not not_2 (not_2_out, S1);
  not not_3 (not_3_out, S0);
  not not_4 (not_4_out, in1);
  not not_5 (not_5_out, in0);
  not not_6 (not_6_out, S3);
  not not_7 (not_7_out, in1);
  not not_8 (not_8_out, in0);
  not not_9 (not_9_out, S3);
  not not_10 (not_10_out, S2);
  not not_11 (not_11_out, in1);
  and and_1 (and_1_out, not_1_out, S2, not_2_out, not_3_out, not_4_out, not_5_out);
  and and_2 (and_2_out, not_6_out, S2, S1, S0, not_7_out, not_8_out);
  and and_3 (out0, not_9_out, not_10_out, S1, S0, not_11_out, in0);
  or or_1 (out1, and_1_out, and_2_out);
endmodule
