// Logisim project P0课上四人表决器.circ as structural Verilog: 2 circuits, main circuit main
module _11 (
  input  [1:0] in_1,
  input  [1:0] in_2,
  input  [1:0] in_3,
  input  [1:0] in_4,
  output Y
);

  wire and_1_out, and_2_out, and_3_out, and_4_out, and_5_out, and_6_out, and_7_out, and_8_out, and_9_out,
       and_10_out, and_11_out, and_12_out, and_13_out, and_14_out, and_15_out, and_16_out, not_1_out,
       not_2_out, not_3_out, not_4_out, not_5_out, not_6_out, not_7_out, not_8_out, not_9_out, not_10_out,
       not_11_out, not_12_out, not_13_out, not_14_out, not_15_out, not_16_out, not_17_out, not_18_out,
       not_19_out, not_20_out, not_21_out, not_22_out, not_23_out, not_24_out, not_25_out, not_26_out,
       not_27_out, not_28_out, not_29_out, not_30_out, not_31_out, not_32_out, not_33_out, not_34_out,
       not_35_out, not_36_out, not_37_out, not_38_out, not_39_out, not_40_out, not_41_out, not_42_out,
       not_43_out, not_44_out, not_45_out, not_46_out, not_47_out, not_48_out, not_49_out, not_50_out,
       not_51_out, not_52_out, not_53_out, not_54_out, not_55_out, not_56_out, not_57_out, not_58_out,
       not_59_out, not_60_out, not_61_out, not_62_out, not_63_out, not_64_out, not_65_out, not_66_out,
       not_67_out, not_68_out, not_69_out, not_70_out, not_71_out, not_72_out, not_73_out, not_74_out,
       not_75_out, not_76_out, not_77_out, not_78_out, not_79_out, not_80_out, not_81_out, not_82_out,
       not_83_out;

  not not_1 (not_1_out, in_1[1]);
  not not_2 (not_2_out, in_1[0]);
  not not_3 (not_3_out, in_2[1]);
  not not_4 (not_4_out, in_2[0]);
  not not_5 (not_5_out, in_3[0]);
  not not_6 (not_6_out, in_1[1]);
  not not_7 (not_7_out, in_1[0]);
  not not_8 (not_8_out, in_2[1]);
  not not_9 (not_9_out, in_2[0]);
  not not_10 (not_10_out, in_4[0]);
  not not_11 (not_11_out, in_1[1]);
  not not_12 (not_12_out, in_1[0]);
  not not_13 (not_13_out, in_2[0]);
  not not_14 (not_14_out, in_3[1]);
  not not_15 (not_15_out, in_3[0]);
  not not_16 (not_16_out, in_1[1]);
  not not_17 (not_17_out, in_1[0]);
  not not_18 (not_18_out, in_2[0]);
  not not_19 (not_19_out, in_3[0]);
  not not_20 (not_20_out, in_4[0]);
  not not_21 (not_21_out, in_1[1]);
  not not_22 (not_22_out, in_1[0]);
  not not_23 (not_23_out, in_2[0]);
  not not_24 (not_24_out, in_4[1]);
  not not_25 (not_25_out, in_4[0]);
  not not_26 (not_26_out, in_1[1]);
  not not_27 (not_27_out, in_1[0]);
  not not_28 (not_28_out, in_3[1]);
  not not_29 (not_29_out, in_3[0]);
  not not_30 (not_30_out, in_4[0]);
  not not_31 (not_31_out, in_1[1]);
  not not_32 (not_32_out, in_1[0]);
  not not_33 (not_33_out, in_3[0]);
  not not_34 (not_34_out, in_4[1]);
  not not_35 (not_35_out, in_4[0]);
  not not_36 (not_36_out, in_1[1]);
  not not_37 (not_37_out, in_2[1]);
  not not_38 (not_38_out, in_2[0]);
  not not_39 (not_39_out, in_3[1]);
  not not_40 (not_40_out, in_3[0]);
  not not_41 (not_41_out, in_4[0]);
  not not_42 (not_42_out, in_1[1]);
  not not_43 (not_43_out, in_2[0]);
  not not_44 (not_44_out, in_3[1]);
  not not_45 (not_45_out, in_3[0]);
  not not_46 (not_46_out, in_4[1]);
  not not_47 (not_47_out, in_4[0]);
  not not_48 (not_48_out, in_1[0]);
  not not_49 (not_49_out, in_2[1]);
  not not_50 (not_50_out, in_2[0]);
  not not_51 (not_51_out, in_3[1]);
  not not_52 (not_52_out, in_3[0]);
  not not_53 (not_53_out, in_1[0]);
  not not_54 (not_54_out, in_2[1]);
  not not_55 (not_55_out, in_2[0]);
  not not_56 (not_56_out, in_3[1]);
  not not_57 (not_57_out, in_4[1]);
  not not_58 (not_58_out, in_4[0]);
  not not_59 (not_59_out, in_1[0]);
  not not_60 (not_60_out, in_2[1]);
  not not_61 (not_61_out, in_2[0]);
  not not_62 (not_62_out, in_3[0]);
  not not_63 (not_63_out, in_4[0]);
  not not_64 (not_64_out, in_1[0]);
  not not_65 (not_65_out, in_2[0]);
  not not_66 (not_66_out, in_3[1]);
  not not_67 (not_67_out, in_3[0]);
  not not_68 (not_68_out, in_4[0]);
  not not_69 (not_69_out, in_1[0]);
  not not_70 (not_70_out, in_2[0]);
  not not_71 (not_71_out, in_3[0]);
  not not_72 (not_72_out, in_4[1]);
  not not_73 (not_73_out, in_4[0]);
  not not_74 (not_74_out, in_1[0]);
  not not_75 (not_75_out, in_3[1]);
  not not_76 (not_76_out, in_3[0]);
  not not_77 (not_77_out, in_4[1]);
  not not_78 (not_78_out, in_4[0]);
  not not_79 (not_79_out, in_1[1]);
  not not_80 (not_80_out, in_1[0]);
  not not_81 (not_81_out, in_2[1]);
  not not_82 (not_82_out, in_3[1]);
  not not_83 (not_83_out, in_3[0]);
  and and_1 (and_1_out, not_1_out, not_2_out, not_3_out, not_4_out, not_5_out);
  and and_2 (and_2_out, not_6_out, not_7_out, not_8_out, not_9_out, not_10_out);
  and and_3 (and_3_out, not_11_out, not_12_out, not_13_out, not_14_out, not_15_out);
  and and_4 (and_4_out, not_16_out, not_17_out, not_18_out, not_19_out, not_20_out);
  and and_5 (and_5_out, not_21_out, not_22_out, not_23_out, not_24_out, not_25_out);
  and and_6 (and_6_out, not_26_out, not_27_out, not_28_out, not_29_out, not_30_out);
  and and_7 (and_7_out, not_31_out, not_32_out, not_33_out, not_34_out, not_35_out);
  and and_8 (and_8_out, not_36_out, not_37_out, not_38_out, not_39_out, not_40_out, not_41_out);
  and and_9 (and_9_out, not_42_out, not_43_out, not_44_out, not_45_out, not_46_out, not_47_out);
  and and_10 (and_10_out, not_48_out, not_49_out, not_50_out, not_51_out, not_52_out);
  and and_11 (and_11_out, not_53_out, not_54_out, not_55_out, not_56_out, not_57_out, not_58_out);
  and and_12 (and_12_out, not_59_out, not_60_out, not_61_out, not_62_out, not_63_out);
  and and_13 (and_13_out, not_64_out, not_65_out, not_66_out, not_67_out, not_68_out);
  and and_14 (and_14_out, not_69_out, not_70_out, not_71_out, not_72_out, not_73_out);
  and and_15 (and_15_out, not_74_out, not_75_out, not_76_out, not_77_out, not_78_out);
  and and_16 (and_16_out, not_79_out, not_80_out, not_81_out, not_82_out, not_83_out, in_4[1]);
  or or_1 (Y, and_1_out, and_2_out, and_3_out, and_4_out, and_5_out, and_6_out, and_7_out, and_8_out, and_9_out, and_10_out, and_11_out, and_12_out, and_13_out, and_14_out, and_15_out, and_16_out);
endmodule

module main (
  input  [1:0] A1,
  input  [1:0] B2,
  input  [1:0] C1,
  input  [1:0] D1,
  output Y
);

  _11 u_11_1 (.in_1(A1), .in_2(B2), .in_3(C1), .in_4(D1), .Y(Y));

  // Notes on the sheet:
  //   A2
  //   B1
  //   C2
  //   D2
endmodule
